# Fritzing sketch predator (saved by Fritzing 0.9.3b)
breadboards: 4

parts:
  Gun = CJMCU-10DOF [form="♀ (female)" package=THT]
  PWM1 = PCA9685 16x12-bit PWM Breakout
  IC1 = L293D [package=THT]
  Pan = Basic Servo
  Tilt = Basic Servo
  LD1 = LD
  Teensy1 = Teensy 3.6 (Basic)
  10DOF1 = CJMCU-10DOF [form="♀ (female)" package=THT]
  DFPlayer_Mini1 = DFPlayer MINI [package="DIP (Dual Inline) [THT]"]
  SP1 = SPEAKER [package=pcb_mount_speaker]
  IC2 = V_REG_LD1117VXX [package=78xxl]
  R1 = Resistor [tolerance=±5% resistance=4.7k package="0805 [SMD]"]
  R2 = Resistor [tolerance=±5% resistance=4.7k package="0805 [SMD]"]
  LED1 = RGB LED (com. cathode, rbg) [package="5 mm [THT]"]
  U1 = RJ45 Jack [package=rj45-8]
  U2 = RJ45 Jack [package=rj45-8]
  Part2 = Arduino Nano (Rev3.0) (ICSP)
  SP2 = SPEAKER [package=pcb_mount_speaker]
  U3 = Mono 2.6W Class D Amplifier [package=8-tdfn-ep]
  U4 = Mono 2.6W Class D Amplifier [package=8-tdfn-ep]
  R3 = Resistor [tolerance=±5% resistance=1k package="0402 [SMD]"]
  LED4 = LED - 3mm [color="Yellow (585nm)" package="3 mm [THT]"]
  LED5 = LED - 3mm [color="Yellow (592nm)" package="3 mm [THT]"]
  R4 = Resistor [tolerance=±5% resistance=100 package="0402 [SMD]"]
  R5 = Resistor [tolerance=±5% resistance=100 package="0402 [SMD]"]
  CONN1 = USB connector [package=THT]
  Part3 = Logic Level Converter
  DFPlayer_Mini2 = DFPlayer MINI [package="DIP (Dual Inline) [THT]"]
  SP4 = SPEAKER [package=pcb_mount_speaker]
  CONN2 = USB connector [package=THT]
  CONN3 = USB connector [package=THT]
  LED7 = smd LED [color="White (8000K)" package="1206 [SMD]"]
  LED8 = smd LED [color="White (8000K)" package="1206 [SMD]"]
  LED9 = smd LED [color="White (8000K)" package="1206 [SMD]"]
  LED10 = smd LED [color="White (8000K)" package="1206 [SMD]"]
  LED11 = smd LED [color="White (8000K)" package="1206 [SMD]"]
  LED12 = smd LED [color="White (8000K)" package="1206 [SMD]"]
  LED13 = smd LED [color="White (8000K)" package="1206 [SMD]"]
  LED14 = smd LED [color="White (8000K)" package="1206 [SMD]"]
  LED15 = smd LED [color="White (8000K)" package="1206 [SMD]"]
  R6 = Resistor [tolerance=±5% resistance=220 package="2010 [SMD]"]
  R7 = Resistor [tolerance=±5% resistance=220 package="2010 [SMD]"]
  R8 = Resistor [tolerance=±5% resistance=220 package="2010 [SMD]"]
  R9 = Resistor [tolerance=±5% resistance=220 package="2010 [SMD]"]
  R10 = Resistor [tolerance=±5% resistance=220 package="2010 [SMD]"]
  R11 = Resistor [tolerance=±5% resistance=220 package="2010 [SMD]"]
  R12 = Resistor [tolerance=±5% resistance=220 package="2010 [SMD]"]
  R13 = Resistor [tolerance=±5% resistance=220 package="2010 [SMD]"]
  R14 = Resistor [tolerance=±5% resistance=220 package="2010 [SMD]"]
  U6 = Mono 2.6W Class D Amplifier [package=8-tdfn-ep]
  U7 = Mono 2.6W Class D Amplifier [package=8-tdfn-ep]
  SP5 = SPEAKER [package=pcb_mount_speaker]
  JP1 = USB_MICROB_PLUG [package=micro-b-th]  # not connected
  Part4 = Arduino Nano (Rev3.0)
  MPU9250_MPU-1 = SparkFun IMU Breakout - MPU-9250 [part_number=" SEN-13762"]
  LD4 = LD
  LD2 = LD
  LD3 = LD
  Part5 = Bluetooth HC-05 Macho
  Part6 = Bluetooth HC-05 Macho
  JP2 = USB_MICROB_PLUG [package=micro-b-th]  # not connected
  R15 = Resistor [tolerance=±5% resistance=1k package="0805 [SMD]"]
  R16 = Resistor [tolerance=±5% resistance=2k package="0603 [SMD]"]

nets:
  N1: Gun.+3V3, Gun.AD0, PWM1.no_name_yet#505, PWM1.no_name_yet#605, U1.3, U1.6
  N2: Gun.GND, PWM1.no_name_yet#501, PWM1.no_name_yet#601, PWM1.no_name_yet#701, PWM1.no_name_yet#1000, PWM1.no_name_yet#1001, PWM1.no_name_yet#1003, PWM1.no_name_yet#1008, PWM1.no_name_yet#1012, IC1.0V, LD1.cathode, LED1.common_cathode, U1.7, U1.8, R6.Pin_1, R7.Pin_1, R8.Pin_1, R9.Pin_1, R10.Pin_1, R11.Pin_1, R12.Pin_1, R13.Pin_1, R14.Pin_1
  N3: Gun.SCL, PWM1.no_name_yet#503, PWM1.no_name_yet#603, U1.5
  N4: Gun.SDA, PWM1.no_name_yet#504, PWM1.no_name_yet#604, U1.4
  N5: PWM1.no_name_yet#3, Tilt.pulse
  N6: PWM1.no_name_yet#5, LED1.blue_anode
  N7: PWM1.no_name_yet#6, LED1.green_anode
  N8: PWM1.no_name_yet#7, LED1.red_anode
  N9: PWM1.no_name_yet#10, IC1.In_4
  N10: PWM1.no_name_yet#11, IC1.In_1
  N11: PWM1.no_name_yet#15, Pan.pulse
  N12: PWM1.no_name_yet#100, PWM1.no_name_yet#103, PWM1.no_name_yet#114, PWM1.no_name_yet#706, IC1.Enable_1, IC1.+Vmotor, IC1.Enable_2, IC1.+V, U1.1, U1.2
  N13: IC1.Out_1_(_Controlled_by_Enable_1_), LD1.anode
  N14: IC1.Out_4_(_Controlled_by_Enable_2_), LED7.anode, LED8.anode, LED9.anode, LED10.anode, LED11.anode, LED12.anode, LED13.anode, LED14.anode, LED15.anode
  GND: Teensy1.GND, Teensy1.GND1, IC2.GND, U2.7, U2.8, Part3.GND, DFPlayer_Mini2.GND, CONN2.GND, CONN2.chassis5, CONN2.chassis6, CONN3.GND, CONN3.chassis6, U6.IN-, U6.GND, U7.IN-, U7.GND, Part5.GND
  N15: Teensy1.D0, DFPlayer_Mini2.TX
  N16: Teensy1.D1, DFPlayer_Mini2.RX
  N17: Teensy1.D2, DFPlayer_Mini2.BUSY
  N18: Teensy1.A4/D18, R1.Pin_1, Part3.TX2_LV
  N19: Teensy1.A5/D19, R2.Pin_1, Part3.RX2_LV
  N20: Teensy1.3V3, Teensy1.3V3_1, IC2.OUT, R1.Pin_0, R2.Pin_0, U2.3, U2.6, Part3.LV
  VCC: Teensy1.Vin, IC2.IN, U2.1, U2.2, Part3.HV, DFPlayer_Mini2.VCC, CONN2.5V, CONN3.5V, U6.VDD, U7.VDD, Part5.VCC
  N21: Teensy1.D34, Part5.TXD
  VDD: 10DOF1.+3V3, DFPlayer_Mini1.VCC, Part2.VIN, U3.VDD, U4.VDD, CONN1.5V
  GND_2: 10DOF1.GND, DFPlayer_Mini1.GND, Part2.GND, U3.IN-, U3.GND, U4.IN-, U4.GND, LED4.cathode, LED5.cathode, CONN1.GND, CONN1.chassis5, CONN1.chassis6, LD4.cathode, LD2.cathode, LD3.cathode
  N22: 10DOF1.SCL, Part2.A5, CONN1.d-
  N23: 10DOF1.SDA, Part2.A4, CONN1.d+
  N24: DFPlayer_Mini1.RX, R3.Pin_1
  N25: DFPlayer_Mini1.TX, Part2.D0/RX
  N26: DFPlayer_Mini1.DAC_R, U3.IN+
  N27: DFPlayer_Mini1.DAC_L, U4.IN+
  N28: DFPlayer_Mini1.BUSY, Part2.D2
  N29: SP1.+, U3.OUT-
  N30: SP1.-, U3.OUT+
  N31: U2.4, Part3.TX2_HV, CONN3.d+
  N32: U2.5, Part3.RX2_HV, CONN3.d-
  N33: Part2.D1/TX, R3.Pin_0
  N34: Part2.D5, LD4.anode, LD2.anode, LD3.anode
  N35: Part2.D9, R5.Pin_1
  N36: Part2.D10, R4.Pin_1
  N37: SP2.+, U4.OUT-
  N38: SP2.-, U4.OUT+
  N39: DFPlayer_Mini2.DAC_R, U6.IN+
  N40: DFPlayer_Mini2.DAC_L, U7.IN+
  N41: SP4.+, U6.OUT-
  N42: SP4.-, U6.OUT+
  N43: U7.OUT-, SP5.+
  N44: U7.OUT+, SP5.-
  N45: Part4.D1/TX, R15.Pin_0
  GND_3: Part4.GND, MPU9250_MPU-1.GND, Part6.Key, R16.Pin_1
  5V: Part4.5V, MPU9250_MPU-1.VDD, Part6.VCC
  N46: Part4.A5, MPU9250_MPU-1.SCL/SCLK
  N47: Part4.A4, MPU9250_MPU-1.SDA/SDI
  N48: Part6.RXD, R15.Pin_1, R16.Pin_0

notes:
  5v servo power rail
  5v signal rail
  Plasma gun
  Box
  Head
  3.3v rail
  5v rail
  USB Power
  USB conn. to the head
  microUSB Power
  USB conn. to the backpack
  Gauntlet
  Wii nunchuck
  HC-06
  miniUSB Power

custom parts:
  CJMCU-10DOF: Placa CJMCU 10DOF basada en conjunto de acelerómetro+giroscopios+magnetómetro MPU-9250 y un barómetro BMP180
  LD: A Generic Red Dot Laser Diode Module (~5mW)
  Teensy 3.6 (Basic): The Teensy is a complete USB-based microcontoller development system, in a very small footprint, capable of implementing many types of projects. All programming is done via the USB port. No special programmer is needed, only a standard micro-USB cable and a PC or Macintosh with a USB port.
  DFPlayer MINI: MP3 module by DFRobot.com for playing Music from an SD-Card. Supports WAV and MP3 files.
